# Fritzing sketch powersupply (saved by Fritzing 0.9.3b)
circuit board: 8.46667cm x 5.64444cm
breadboards: 1

parts:
  D3 = Rectifier Diode [part_number=1N4001 package="300 mil [THT]"]
  C1 = Tantalum Capacitor [capacitance=47µF voltage=10V package="100 mil [THT, tantalum]"]
  R1 = Resistor [tolerance=±1% resistance=3.3M package=THT]
  R2 = Resistor [tolerance=±1% resistance=100 package=THT]
  S1 = Square Pushbutton
  R3 = Resistor [tolerance=±1% resistance=10k package=THT]
  Q2 = MOSFET-NCHANNEL [package=to220v]
  LM1 = RioRand LM2596
  JP1 = Header 4 [package=jst-4-pth]
  IC1 = General purpose bipolar Timer [package=dil-08]
  D2 = Rectifier Diode [part_number=1N4001 package="300 mil [THT]"]

nets:
  N1: D3.cathode, R3.Pin_1, Q2.G, D2.cathode
  N2: D3.anode, IC1.OUT
  GND: C1.-, S1.leg0, R3.Pin_0, Q2.S, IC1.GND
  N3: C1.+, R1.Pin_0, R2.Pin_0, IC1.TRI, IC1.TRE
  9V: R1.Pin_1, LM1.Pin_0, JP1.2, IC1._RES, IC1.VCC+
  N4: R2.Pin_1, S1.leg1
  N5: Q2.D, LM1.Pin_1
  N6: LM1.Pin_2, JP1.3
  N7: LM1.Pin_3, JP1.4
  N8: JP1.1, D2.anode

notes:
  +5 V Power Supply for Raspberry Pi
  Voltage Control
  Raspi Pin GPIO17 (Phys #11)
